// Logisim project MOJ10_lab10.circ as structural Verilog: 4 circuits, main circuit main
module main (
  input  RoadDetectorNS,
  input  RoadDetectorEW
);

  wire clk_out, fsm_canvas_1_ewlight, fsm_canvas_1_nslight;

  Clock clk (.out(clk_out));
  FSM_Canvas fsm_canvas_1 (
    .clock(clk_out), .RoadDetectorNS(RoadDetectorNS), .RoadDetectorEW(RoadDetectorEW),
    .NSlight(fsm_canvas_1_nslight), .EWlight(fsm_canvas_1_ewlight));
  LED NSLite (.in(fsm_canvas_1_nslight));
  LED EWLite (.in(fsm_canvas_1_ewlight));
endmodule

module Output (
  input  CurrentState,
  output EWlite,
  output NSlite
);

  not not_1 (NSlite, CurrentState);

  assign EWlite = CurrentState;
endmodule

module FSM_Canvas (
  input  clock,
  input  RoadDetectorNS,
  input  RoadDetectorEW,
  output NSlight,
  output EWlight
);

  wire register_1_q, state_transition_1_nextstate;

  Register #(.width(1)) register_1 (.D(state_transition_1_nextstate), .Q(register_1_q), .clk(clock));  // open: en, clr
  State_Transition state_transition_1 (
    .CurrentState(register_1_q), .NSCar(RoadDetectorNS), .EWCar(RoadDetectorEW),
    .NextState(state_transition_1_nextstate));
  Output output_1 (.CurrentState(register_1_q), .EWlite(EWlight), .NSlite(NSlight));
endmodule

module State_Transition (
  input  CurrentState,
  input  NSCar,
  input  EWCar,
  output NextState
);

  wire and_1_out, and_2_out, not_1_out, not_2_out;

  not not_1 (not_1_out, NSCar);
  not not_2 (not_2_out, CurrentState);
  and and_1 (and_1_out, not_2_out, EWCar);
  and and_2 (and_2_out, CurrentState, not_1_out);
  or or_1 (NextState, and_1_out, and_2_out);
endmodule
