// Logisim project MOJ10_lab11.circ as structural Verilog: 3 circuits, main circuit main
module main (
  input  clear,
  output [31:0] \output 
);

  wire clock_1_out, clock_2_out;
  wire [1:0] bit_extender_2_out, bit_extender_3_out;
  wire [4:0] decode_1_rs, decode_1_rt, subtractor_1_out, subtractor_2_out;
  wire [7:0] adder_1_out, Program_Counter_q;
  wire [15:0] decode_1_immediate;
  wire [31:0] bit_extender_1_out, rom_1_data;

  Clock clock_1 (.out(clock_1_out));
  Decode decode_1 (
    .Current_State(rom_1_data), .immediate(decode_1_immediate), .rt(decode_1_rt), .rs(decode_1_rs));  // open: opcode
  ROM #(.dataWidth(32)) rom_1 (.addr(Program_Counter_q), .data(rom_1_data));  // open: sel
  Register Program_Counter (.D(adder_1_out), .Q(Program_Counter_q), .clk(clock_1_out), .clr(clear));  // open: en
  Adder adder_1 (.a(Program_Counter_q), .b(8'h1), .out(adder_1_out));  // open: cin, cout
  assign bit_extender_1_out = {{16{decode_1_immediate[15]}}, decode_1_immediate};  // Bit_Extender bit_extender_1
  Subtractor #(.width(5)) subtractor_1 (.a(decode_1_rt), .b(5'b01000), .out(subtractor_1_out));  // open: bin, bout
  Subtractor #(.width(5)) subtractor_2 (.a(decode_1_rs), .b(5'b01000), .out(subtractor_2_out));  // open: bin, bout
  Bit_Extender #(.in_width(5), .out_width(2)) bit_extender_2 (.in(subtractor_1_out), .out(bit_extender_2_out));
  Clock clock_2 (.out(clock_2_out));
  Bit_Extender #(.in_width(5), .out_width(2)) bit_extender_3 (.in(subtractor_2_out), .out(bit_extender_3_out));
  Register_File register_file_1 (
    .data_to_write(bit_extender_1_out), .clock(clock_2_out), .write_register(bit_extender_2_out),
    .read_register(bit_extender_3_out), .read_data(\output ));

  // Notes on the sheet:
  //   contents of rom_1 (hex, n*v repeats v):
  //   21080004 2129000a 210a0006 212bfffb
endmodule

module Register_File (
  input  [31:0] data_to_write,
  input  clock,
  input  [1:0] write_register,
  input  [1:0] read_register,
  output [31:0] read_data
);

  wire decoder_1_out0, decoder_1_out1, decoder_1_out2, decoder_1_out3;
  wire [31:0] t0_q, t1_q, t2_q, t3_q;

  Decoder #(.select(2), .enable("false")) decoder_1 (
    .out0(decoder_1_out0), .out1(decoder_1_out1), .out2(decoder_1_out2), .out3(decoder_1_out3),
    .sel(write_register));
  Register #(.width(32)) t0 (.D(data_to_write), .en(decoder_1_out0), .Q(t0_q), .clk(clock));  // open: clr
  Register #(.width(32)) t1 (.D(data_to_write), .en(decoder_1_out1), .Q(t1_q), .clk(clock));  // open: clr
  Register #(.width(32)) t2 (.D(data_to_write), .en(decoder_1_out2), .Q(t2_q), .clk(clock));  // open: clr
  Register #(.width(32)) t3 (.D(data_to_write), .en(decoder_1_out3), .Q(t3_q), .clk(clock));  // open: clr
  Multiplexer #(.select(2), .width(32), .enable("false")) multiplexer_1 (
    .in0(t0_q), .in1(t1_q), .in2(t2_q), .in3(t3_q), .out(read_data), .sel(read_register));
endmodule

module Decode (
  input  [31:0] Current_State,
  output [15:0] immediate,
  output [4:0] rt,
  output [4:0] rs,
  output [5:0] opcode
);


  assign immediate = Current_State[15:0];
  assign opcode = Current_State[31:26];
  assign rs = Current_State[25:21];
  assign rt = Current_State[20:16];
endmodule
