// Logisim project MOJ10_lab6.circ as structural Verilog: 1 circuit, main circuit main
module main (
  input  [7:0] Input,
  input  [15:0] Output
);


  assign Output = {{9{Input[7]}}, Input[6:0]};
endmodule
