// Logisim project MOJ10_lab7.circ as structural Verilog: 1 circuit, main circuit main
module main (
  input  A,
  input  B,
  input  C,
  input  A_2,
  input  B_2,
  input  C_2,
  output Cout,
  output Sum
);

  wire and_1_out, and_2_out, and_3_out, and_4_out, and_5_out, and_6_out, and_7_out, and_8_out, not_1_out,
       not_2_out, not_3_out, not_4_out, not_5_out, not_6_out, or_1_out, or_2_out, or_4_out, or_5_out;

  not not_1 (not_1_out, A);
  not not_2 (not_2_out, B);
  not not_3 (not_3_out, C);
  not not_4 (not_4_out, A_2);
  not not_5 (not_5_out, B_2);
  not not_6 (not_6_out, C_2);
  and and_1 (and_1_out, not_1_out, B, C);
  and and_2 (and_2_out, A, B, C);
  and and_3 (and_3_out, not_2_out, C, A);
  and and_4 (and_4_out, not_3_out, A, B);
  and and_5 (and_5_out, A_2, B_2, C_2);
  and and_6 (and_6_out, not_4_out, not_5_out, C_2);
  and and_7 (and_7_out, not_4_out, B_2, not_6_out);
  and and_8 (and_8_out, A_2, not_5_out, not_6_out);
  or or_1 (or_1_out, and_1_out, and_2_out);
  or or_2 (or_2_out, and_3_out, and_4_out);
  or or_3 (Cout, or_1_out, or_2_out);
  or or_4 (or_4_out, and_5_out, and_6_out);
  or or_5 (or_5_out, and_7_out, and_8_out);
  or or_6 (Sum, or_4_out, or_5_out);
endmodule
