// Logisim project MOJ10_lab8.circ as structural Verilog: 2 circuits, main circuit main
module main (
  input  enable_write,
  input  [7:0] \input ,
  input  select,
  output [7:0] register_contents
);

  wire clock_out;
  wire [7:0] adder_1_out, multiplexer_1_out;

  Clock clock (.out(clock_out));
  Multiplexer #(.width(8), .enable("false")) multiplexer_1 (
    .in0(\input ), .in1(adder_1_out), .out(multiplexer_1_out), .sel(select));
  register \reg  (.Enable_Write(enable_write), .\input (multiplexer_1_out), .\output (register_contents));
  Adder adder_1 (.a(8'h1), .b(register_contents), .out(adder_1_out));  // open: cin, cout
endmodule

module register (
  input  Enable_Write,
  input  [7:0] \input ,
  output [7:0] \output 
);

  wire clock_out;

  Clock clock (.out(clock_out));
  D_Flip_Flop d_ff_1 (.clk(clock_out), .D(\input [0]), .Q(\output [0]), .en(Enable_Write));  // open: Qn, preset, reset
  D_Flip_Flop d_ff_2 (.clk(clock_out), .D(\input [1]), .Q(\output [1]), .en(Enable_Write));  // open: Qn, preset, reset
  D_Flip_Flop d_ff_3 (.clk(clock_out), .D(\input [2]), .Q(\output [2]), .en(Enable_Write));  // open: Qn, preset, reset
  D_Flip_Flop d_ff_4 (.clk(clock_out), .D(\input [3]), .Q(\output [3]), .en(Enable_Write));  // open: Qn, preset, reset
  D_Flip_Flop d_ff_5 (.clk(clock_out), .D(\input [4]), .Q(\output [4]), .en(Enable_Write));  // open: Qn, preset, reset
  D_Flip_Flop d_ff_6 (.clk(clock_out), .D(\input [5]), .Q(\output [5]), .en(Enable_Write));  // open: Qn, preset, reset
  D_Flip_Flop d_ff_7 (.clk(clock_out), .D(\input [6]), .Q(\output [6]), .en(Enable_Write));  // open: Qn, preset, reset
  D_Flip_Flop d_ff_8 (.clk(clock_out), .D(\input [7]), .Q(\output [7]), .en(Enable_Write));  // open: Qn, preset, reset
endmodule
