// Logisim project MOJ10_lab9.circ as structural Verilog: 2 circuits, main circuit main
module main (
  input  [7:0] data_to_write,
  input  [1:0] write_reg,
  input  [1:0] read_reg,
  output [7:0] read_data
);

  wire clock_1_out;

  Clock clock_1 (.out(clock_1_out));
  \new  new_1 (
    .data_to_write(data_to_write), .clock(clock_1_out), .write_register(write_reg), .read_register(read_reg),
    .read_data(read_data));
endmodule

module \new  (
  input  [7:0] data_to_write,
  input  clock,
  input  [1:0] write_register,
  input  [1:0] read_register,
  output [7:0] read_data
);

  wire decoder_1_out0, decoder_1_out1, decoder_1_out2, decoder_1_out3;
  wire [7:0] t0_q, t1_q, t2_q, t3_q;

  Decoder #(.select(2), .enable("false")) decoder_1 (
    .out0(decoder_1_out0), .out1(decoder_1_out1), .out2(decoder_1_out2), .out3(decoder_1_out3),
    .sel(write_register));
  Register t0 (.D(data_to_write), .en(decoder_1_out0), .Q(t0_q), .clk(clock));  // open: clr
  Register t1 (.D(data_to_write), .en(decoder_1_out1), .Q(t1_q), .clk(clock));  // open: clr
  Register t2 (.D(data_to_write), .en(decoder_1_out2), .Q(t2_q), .clk(clock));  // open: clr
  Register t3 (.D(data_to_write), .en(decoder_1_out3), .Q(t3_q), .clk(clock));  // open: clr
  Multiplexer #(.select(2), .width(8), .enable("false")) multiplexer_1 (
    .in0(t0_q), .in1(t1_q), .in2(t2_q), .in3(t3_q), .out(read_data), .sel(read_register));
endmodule
