// Logisim project door FSM.circ as structural Verilog: 4 circuits, main circuit main
module main (
  input  Sensor,
  input  Endstop,
  input  Timer
);

  wire clock_1_out, decoder_1_out0, decoder_1_out1, decoder_1_out2, decoder_1_out3, door_fsm_1_d,
       door_fsm_1_p;
  wire [1:0] door_fsm_1_state;

  Clock clock_1 (.out(clock_1_out));
  Door_FSM door_fsm_1 (
    .CLK(clock_1_out), .Sensor(Sensor), .Endstop(Endstop), .Timer(Timer), .State(door_fsm_1_state),
    .P(door_fsm_1_p), .D(door_fsm_1_d));
  LED Closed (.in(decoder_1_out0));
  LED Opening (.in(decoder_1_out1));
  LED Open (.in(decoder_1_out2));
  Decoder #(.select(2), .enable("false")) decoder_1 (
    .out0(decoder_1_out0), .out1(decoder_1_out1), .out2(decoder_1_out2), .out3(decoder_1_out3),
    .sel(door_fsm_1_state));
  LED Closing (.in(decoder_1_out3));
  LED Motor_Power (.in(door_fsm_1_p));
  LED Motor_Opening (.in(door_fsm_1_d));

  // Notes on the sheet:
  //   This state display is just
  //   for illustration.
  //   These are the only two "real" outputs.
endmodule

module Door_State_Transition (
  input  S0,
  input  S1,
  input  S,
  input  E,
  input  T,
  output S0_2,
  output S1_2
);

  wire and_1_out, and_2_out, and_3_out, and_4_out, and_5_out, and_6_out, not_1_out, not_2_out, not_3_out,
       not_4_out, not_5_out, not_6_out, not_7_out, not_8_out, not_9_out;

  not not_1 (not_1_out, S0);
  not not_2 (not_2_out, S1);
  not not_3 (not_3_out, S);
  not not_4 (not_4_out, E);
  not not_5 (not_5_out, S0);
  not not_6 (not_6_out, S1);
  not not_7 (not_7_out, E);
  not not_8 (not_8_out, S1);
  not not_9 (not_9_out, S);
  and and_1 (and_1_out, not_1_out, S1, E);
  and and_2 (and_2_out, S0, not_2_out);
  and and_3 (and_3_out, S0, not_3_out, not_4_out);
  and and_4 (and_4_out, not_5_out, not_6_out, S);
  and and_5 (and_5_out, S1, not_7_out);
  and and_6 (and_6_out, S0, not_8_out, not_9_out, T);
  or or_1 (S0_2, and_1_out, and_2_out, and_3_out);
  or or_2 (S1_2, and_4_out, and_5_out, and_6_out);
endmodule

module Door_Output (
  input  S0,
  input  S1,
  output P,
  output D
);

  and and_1 (D, ~S0, S1);  // AND_Gate

  assign P = S1;
endmodule

module Door_FSM (
  input  CLK,
  input  Sensor,
  input  Endstop,
  input  Timer,
  output [1:0] State,
  output P,
  output D
);

  wire NewS0, NewS1;

  D_Flip_Flop d_ff_1 (.clk(CLK), .D(NewS1), .Q(State[1]));  // open: Qn, preset, en, reset
  D_Flip_Flop d_ff_2 (.clk(CLK), .D(NewS0), .Q(State[0]));  // open: Qn, preset, en, reset
  Door_Output door_output_1 (.S0(State[1]), .S1(State[0]), .P(P), .D(D));
  Door_State_Transition door_state_transition_1 (
    .S0(State[1]), .S1(State[0]), .S(Sensor), .E(Endstop), .T(Timer), .S0_2(NewS1), .S1_2(NewS0));
endmodule
