// Logisim project MOJ10_JrMips.circ as structural Verilog
module main (
);

  wire button_1_out, CLK, clock_1_out, control_1_halt, control_1_put, control_1_regwrite,
       control_1_signedorunsigned, not_1_out;
  wire [1:0] control_1_branch, control_1_memtorg, control_1_pcsrc, control_1_rtorimm;
  wire [2:0] control_1_aluop, fields_1_rs, fields_1_rt;
  wire [3:0] fields_1_shamt, register_2_q_2, register_2_q_3;
  wire [7:0] adder_1_out, bit_extender_1_out, bit_extender_2_out, bit_extender_3_out, multiplexer_1_out,
       register_1_q, register_2_q;
  wire [15:0] alu_1_output, bit_extender_4_out, bit_extender_5_out, bit_extender_6_out, fields_1_immediate,
       jump_control_1_output_pc, multiplexer_2_out, multiplexer_3_out, multiplexer_4_out, ram_1_data,
       RG_read_data, RG_read_data_2, rom_1_data;

  LED halt (.in(control_1_halt));
  Multiplexer #(.select(2), .width(8), .enable("false")) multiplexer_1 (
    .in0(adder_1_out), .in1(bit_extender_1_out), .in2(bit_extender_3_out), .in3(bit_extender_2_out),
    .out(multiplexer_1_out), .sel(control_1_pcsrc));
  Register register_1 (.D(multiplexer_1_out), .en(not_1_out), .Q(register_1_q), .clk(CLK));  // open: clr
  Bit_Extender #(.in_width(16), .out_width(8)) bit_extender_1 (.in(fields_1_immediate), .out(bit_extender_1_out));
  not not_1 (not_1_out, control_1_halt);
  Bit_Extender #(.in_width(16), .out_width(8)) bit_extender_2 (.in(jump_control_1_output_pc), .out(bit_extender_2_out));
  Bit_Extender #(.in_width(16), .out_width(8)) bit_extender_3 (.in(RG_read_data), .out(bit_extender_3_out));
  assign bit_extender_4_out = {{8{bit_extender_1_out[7]}}, bit_extender_1_out};  // Bit_Extender bit_extender_4
  Jump_Control jump_control_1 (
    .Input_PC(rom_1_data), .Target_address(fields_1_immediate), .Output_PC(jump_control_1_output_pc));  // open: Jump
  Adder adder_1 (.a(8'h1), .b(register_1_q), .out(adder_1_out));  // open: cin, cout
  assign bit_extender_5_out = {{8{1'b0}}, register_1_q};  // Bit_Extender bit_extender_5
  ROM #(.dataWidth(16)) rom_1 (.addr(register_1_q), .data(rom_1_data));  // open: sel
  Fields fields_1 (
    .Instruction(rom_1_data), .rs(fields_1_rs), .rt(fields_1_rt), .shamt(fields_1_shamt),
    .Immediate(fields_1_immediate));  // open: Opcode_sub
  Button button_1 (.out(button_1_out));
  Clock clock_1 (.out(clock_1_out));
  assign bit_extender_6_out = {{12{1'b0}}, fields_1_shamt};  // Bit_Extender bit_extender_6
  or or_1 (CLK, button_1_out, clock_1_out);
  Multiplexer #(.width(16), .enable("false")) multiplexer_2 (
    .in0(bit_extender_4_out), .in1(fields_1_immediate), .out(multiplexer_2_out),
    .sel(control_1_signedorunsigned));
  Multiplexer #(.select(2), .width(16), .enable("false")) multiplexer_3 (
    .in0(ram_1_data), .in1(alu_1_output), .in2(bit_extender_5_out), .in3(multiplexer_2_out),
    .out(multiplexer_3_out), .sel(control_1_memtorg));
  Control control_1 (
    .in_1(rom_1_data), .ALUOP(control_1_aluop), .RegWrite(control_1_regwrite), .PCSrc(control_1_pcsrc),
    .MemToRG(control_1_memtorg), .put(control_1_put), .signedorunsigned(control_1_signedorunsigned),
    .rtORimm(control_1_rtorimm), .halt(control_1_halt), .branch(control_1_branch));
  Jr jr_1 ();  // open: Input_PC, rs, Jump, Output_PC
  RegisterFile RG (
    .data_to_write(multiplexer_3_out), .clock(CLK), .read_data(RG_read_data), .write_register(fields_1_rs),
    .read_register(fields_1_rt), .read_register_2(fields_1_rs), .read_data_2(RG_read_data_2),
    .write_enable(control_1_regwrite));
  Multiplexer #(.select(2), .width(16), .enable("false")) multiplexer_4 (
    .in0(RG_read_data_2), .in1(multiplexer_2_out), .in2(bit_extender_6_out), .out(multiplexer_4_out),
    .sel(control_1_rtorimm));  // open: in3
  ALU alu_1 (
    .input1(RG_read_data), .\output (alu_1_output), .input2(multiplexer_4_out), .in_4(control_1_aluop),
    .in_2(control_1_branch));  // open: Zero
  Hex_Digit_Display hex_digit_display_1 (.value(register_2_q_3));  // open: dp
  Register #(.width(16)) register_2 (
    .D(RG_read_data), .en(control_1_put), .Q({register_2_q_3, register_2_q_2, register_2_q}), .clk(CLK));  // open: clr
  Hex_Digit_Display hex_digit_display_2 (.value(register_2_q[7:4]));  // open: dp
  Hex_Digit_Display hex_digit_display_3 (.value(register_2_q_2));  // open: dp
  Hex_Digit_Display hex_digit_display_4 (.value(register_2_q[3:0]));  // open: dp
  RAM #(.dataWidth(16)) ram_1 (.addr(RG_read_data_2[7:0]), .data(ram_1_data), .clk(CLK));  // open: sel, ld, clr

  // Notes on the sheet:
  //   contents of rom_1 (hex, n*v repeats v):
  //   2002 23fc 2407 2609 1000 1200 1400 1600 3040 1000 3681 1600 2002 4140 1000 4081 1000 2000 1000 500b
  //   51fe 200a 2404 6081 1000 500a 1000 6080 1000 2002 2206 1000 70c0 1000 70c1 1000 8004 1000 8005 1000
endmodule

module ALU (
  input  [15:0] input1,
  input  [1:0] in_2,
  input  [15:0] input2,
  input  [2:0] in_4,
  output Zero,
  output [15:0] \output 
);

  wire comparator_1_eq, comparator_1_gt, comparator_1_lt, not_1_out;
  wire [15:0] adder_1_out, and_1_out, nor_1_out, shifter_1_out, shifter_2_out, subtractor_1_out;

  Adder #(.width(16)) adder_1 (.a(input1), .b(input2), .out(adder_1_out));  // open: cin, cout
  Subtractor #(.width(16)) subtractor_1 (.a(input2), .b(input1), .out(subtractor_1_out));  // open: bin, bout
  assign and_1_out = input1 & input2;  // AND_Gate and_1, 16 bits wide
  assign nor_1_out = ~(input1 | input2);  // NOR_Gate nor_1, 16 bits wide
  Shifter #(.width(16)) shifter_1 (.in(input1), .\dist (input2[3:0]), .out(shifter_1_out));
  Shifter #(.width(16), .shift("lr")) shifter_2 (.in(input1), .\dist (input2[3:0]), .out(shifter_2_out));
  Multiplexer #(.select(3), .width(16), .enable("false")) multiplexer_1 (
    .in0(adder_1_out), .in1(subtractor_1_out), .in2(and_1_out), .in3(nor_1_out), .in4(shifter_1_out),
    .in5(shifter_2_out), .out(\output ), .sel(in_4));  // open: in6, in7
  Comparator #(.width(16)) comparator_1 (
    .a(input1), .b({16{1'b0}}), .gt(comparator_1_gt), .eq(comparator_1_eq), .lt(comparator_1_lt));
  not not_1 (not_1_out, comparator_1_eq);
  Multiplexer #(.select(2), .enable("false")) multiplexer_2 (
    .in0(comparator_1_gt), .in1(comparator_1_lt), .in2(comparator_1_eq), .in3(not_1_out), .out(Zero),
    .sel(in_2));
endmodule

module RegisterFile (
  input  [15:0] data_to_write,
  input  clock,
  input  write_enable,
  input  [2:0] read_register,
  input  [2:0] write_register,
  input  [2:0] read_register_2,
  output [15:0] read_data,
  output [15:0] read_data_2
);

  wire demultiplexer_1_out0, demultiplexer_1_out1, demultiplexer_1_out2, demultiplexer_1_out3,
       demultiplexer_1_out4, demultiplexer_1_out5, demultiplexer_1_out6, demultiplexer_1_out7;
  wire [15:0] t0_q, t1_q, t2_q, t3_q, t4_q, t5_q, t6_q, t7_q;

  Demultiplexer #(.select(3)) demultiplexer_1 (
    .out0(demultiplexer_1_out0), .out1(demultiplexer_1_out1), .out2(demultiplexer_1_out2),
    .out3(demultiplexer_1_out3), .out4(demultiplexer_1_out4), .out5(demultiplexer_1_out5),
    .out6(demultiplexer_1_out6), .out7(demultiplexer_1_out7), .in(write_enable), .sel(write_register));  // open: en
  Register #(.width(16)) t0 (.D(data_to_write), .en(demultiplexer_1_out0), .Q(t0_q), .clk(clock));  // open: clr
  Register #(.width(16)) t1 (.D(data_to_write), .en(demultiplexer_1_out1), .Q(t1_q), .clk(clock));  // open: clr
  Register #(.width(16)) t2 (.D(data_to_write), .en(demultiplexer_1_out2), .Q(t2_q), .clk(clock));  // open: clr
  Register #(.width(16)) t3 (.D(data_to_write), .en(demultiplexer_1_out3), .Q(t3_q), .clk(clock));  // open: clr
  Register #(.width(16)) t4 (.D(data_to_write), .en(demultiplexer_1_out4), .Q(t4_q), .clk(clock), .clr(clock));
  Register #(.width(16)) t5 (.D(data_to_write), .en(demultiplexer_1_out5), .Q(t5_q), .clk(clock));  // open: clr
  Register #(.width(16)) t6 (.D(data_to_write), .en(demultiplexer_1_out6), .Q(t6_q), .clk(clock));  // open: clr
  Register #(.width(16)) t7 (.D(data_to_write), .en(demultiplexer_1_out7), .Q(t7_q), .clk(clock));  // open: clr
  Multiplexer #(.select(3), .width(16), .enable("false")) multiplexer_1 (
    .in0(t0_q), .in1(t1_q), .in2(t2_q), .in3(t3_q), .in4(t4_q), .in5(t5_q), .in6(t6_q), .in7(t7_q),
    .out(read_data), .sel(read_register));
  Multiplexer #(.select(3), .width(16), .enable("false")) multiplexer_2 (
    .in0(t0_q), .in1(t1_q), .in2(t2_q), .in3(t3_q), .in4(t4_q), .in5(t5_q), .in6(t6_q), .in7(t7_q),
    .out(read_data_2), .sel(read_register_2));
endmodule

module ALUOP (
  input  [4:0] Op_Sub,
  output [2:0] ALUOP
);

  wire and_1_out, and_3_out, and_4_out, not_1_out, not_2_out, not_3_out;

  and and_1 (and_1_out, Op_Sub[3], Op_Sub[2]);
  not not_1 (not_1_out, Op_Sub[4]);
  not not_2 (not_2_out, Op_Sub[1]);
  not not_3 (not_3_out, Op_Sub[1]);
  or or_1 (ALUOP[2], and_1_out, Op_Sub[4]);
  and and_2 (ALUOP[1], not_1_out, not_2_out);
  and and_3 (and_3_out, not_3_out, Op_Sub[0]);
  and and_4 (and_4_out, Op_Sub[2], Op_Sub[0]);
  or or_2 (ALUOP[0], and_3_out, and_4_out);
endmodule

module put (
  input  [4:0] put,
  output out_2
);

  and and_1 (out_2, ~put[4], ~put[3], ~put[2], put[1], ~put[0]);  // AND_Gate
endmodule

module Control (
  input  [15:0] in_1,
  output [2:0] ALUOP,
  output put,
  output [1:0] MemToRG,
  output RegWrite,
  output [1:0] PCSrc,
  output signedorunsigned,
  output [1:0] rtORimm,
  output halt,
  output [1:0] branch
);

  wire [4:0] fields_1_opcode_sub;

  Fields fields_1 (.Instruction(in_1), .Opcode_sub(fields_1_opcode_sub));  // open: rs, rt, shamt, Immediate
  put put_1 (.put(fields_1_opcode_sub), .out_2(put));
  MemoryToRG memorytorg_1 (.opsub(fields_1_opcode_sub), .memtorg(MemToRG));
  RegWrite regwrite_1 (.Op_Sub(fields_1_opcode_sub), .WriteORNot(RegWrite));
  PCSrc pcsrc_1 (.Op_Sub(fields_1_opcode_sub), .PCSrc(PCSrc));
  immediate immediate_1 (.opsub(fields_1_opcode_sub), .signedounon(signedorunsigned));
  rtORimm rtorimm_1 (.Op_Sub(fields_1_opcode_sub), .rt(rtORimm));
  halt halt_1 (.Op_Sub(fields_1_opcode_sub), .halt(halt));
  branch_control branch_control_1 (.Op_Sub(fields_1_opcode_sub), .branch(branch));
  ALUOP aluop_1 (.Op_Sub(fields_1_opcode_sub), .ALUOP(ALUOP));
endmodule

module PCSrc (
  input  [4:0] Op_Sub,
  output [1:0] PCSrc
);

  wire and_2_out, and_3_out, and_4_out, not_1_out, not_2_out, not_3_out;

  not not_1 (not_1_out, Op_Sub[3]);
  not not_2 (not_2_out, Op_Sub[2]);
  not not_3 (not_3_out, Op_Sub[0]);
  and and_1 (PCSrc[1], not_1_out, not_2_out, Op_Sub[1], Op_Sub[0]);
  and and_2 (and_2_out, Op_Sub[4], Op_Sub[1], not_3_out);
  and and_3 (and_3_out, Op_Sub[4], Op_Sub[2]);
  and and_4 (and_4_out, Op_Sub[4], Op_Sub[3]);
  or or_1 (PCSrc[0], and_2_out, and_3_out, and_4_out);
endmodule

module RegWrite (
  input  [4:0] Op_Sub,
  output WriteORNot
);

  wire and_1_out, and_2_out, and_3_out, and_4_out, and_5_out, not_1_out, not_2_out, not_3_out, not_4_out,
       not_5_out, not_6_out, not_7_out, not_8_out;

  not not_1 (not_1_out, Op_Sub[4]);
  not not_2 (not_2_out, Op_Sub[3]);
  not not_3 (not_3_out, Op_Sub[4]);
  not not_4 (not_4_out, Op_Sub[2]);
  not not_5 (not_5_out, Op_Sub[4]);
  not not_6 (not_6_out, Op_Sub[0]);
  not not_7 (not_7_out, Op_Sub[3]);
  not not_8 (not_8_out, Op_Sub[1]);
  and and_1 (and_1_out, not_1_out, not_2_out, Op_Sub[2]);
  and and_2 (and_2_out, not_3_out, Op_Sub[3], not_4_out);
  and and_3 (and_3_out, not_5_out, Op_Sub[3], not_6_out);
  and and_4 (and_4_out, Op_Sub[3], Op_Sub[1]);
  and and_5 (and_5_out, Op_Sub[4], not_7_out, not_8_out);
  or or_1 (WriteORNot, and_1_out, and_2_out, and_3_out, and_4_out, and_5_out);
endmodule

// Jump
module Jump_Control (
  input  [15:0] Input_PC,
  input  [15:0] Target_address,
  input  Jump,
  output [15:0] Output_PC
);

  Multiplexer #(.width(16), .enable("false")) multiplexer_1 (
    .in0(Input_PC), .in1(Target_address), .out(Output_PC), .sel(Jump));
endmodule

module Fields (
  input  [15:0] Instruction,
  output [4:0] Opcode_sub,
  output [2:0] rs,
  output [2:0] rt,
  output [3:0] shamt,
  output [15:0] Immediate
);

  assign Immediate = {{8{1'b0}}, Instruction[8:1]};  // Bit_Extender bit_extender_1

  assign Opcode_sub = {Instruction[15:12], Instruction[0]};
  assign rs = Instruction[11:9];
  assign rt = Instruction[8:6];
  assign shamt = Instruction[4:1];
endmodule

module Jr (
  input  [15:0] Input_PC,
  input  [2:0] rs,
  input  Jump,
  output [15:0] Output_PC
);

  wire [15:0] bit_extender_1_out;

  assign bit_extender_1_out = {{13{1'b0}}, rs};  // Bit_Extender bit_extender_1
  Multiplexer #(.width(16), .enable("false")) multiplexer_1 (
    .in0(Input_PC), .in1(bit_extender_1_out), .out(Output_PC), .sel(Jump));
endmodule

module MemoryToRG (
  input  [4:0] opsub,
  output [1:0] memtorg
);

  wire and_2_out, not_1_out, not_2_out, not_3_out, not_4_out, not_5_out;

  not not_1 (not_1_out, opsub[3]);
  not not_2 (not_2_out, opsub[1]);
  not not_3 (not_3_out, opsub[4]);
  not not_4 (not_4_out, opsub[3]);
  and and_1 (memtorg[1], not_1_out, opsub[2], not_2_out);
  and and_2 (and_2_out, not_3_out, not_4_out);
  not not_5 (not_5_out, opsub[2]);
  or or_1 (memtorg[0], and_2_out, not_5_out, opsub[1]);
endmodule

module immediate (
  input  [4:0] opsub,
  output signedounon
);

  not not_1 (signedounon, opsub[4]);
endmodule

module rtORimm (
  input  [4:0] Op_Sub,
  output [1:0] rt
);

  wire not_1_out;

  not not_1 (not_1_out, Op_Sub[2]);
  and and_1 (rt[0], not_1_out, Op_Sub[1]);

  assign rt[1] = Op_Sub[4];
endmodule

module halt (
  input  [4:0] Op_Sub,
  output halt
);

  wire not_1_out, not_2_out, not_3_out, not_4_out, not_5_out;

  not not_1 (not_1_out, Op_Sub[4]);
  not not_2 (not_2_out, Op_Sub[3]);
  not not_3 (not_3_out, Op_Sub[2]);
  not not_4 (not_4_out, Op_Sub[1]);
  not not_5 (not_5_out, Op_Sub[0]);
  and and_1 (halt, not_1_out, not_2_out, not_3_out, not_4_out, not_5_out);
endmodule

module branch_control (
  input  [4:0] Op_Sub,
  output [1:0] branch
);

  wire and_1_out, and_2_out, not_2_out, not_3_out, not_4_out;

  not not_1 (branch[1], Op_Sub[2]);
  not not_2 (not_2_out, Op_Sub[2]);
  not not_3 (not_3_out, Op_Sub[0]);
  not not_4 (not_4_out, Op_Sub[3]);
  and and_1 (and_1_out, not_2_out, not_3_out);
  and and_2 (and_2_out, not_4_out, Op_Sub[0]);
  or or_1 (branch[0], and_1_out, and_2_out);
endmodule
